// Logisim project Practica4.circ as structural Verilog
module Semisumador1Bit (
  input  X,
  input  Y,
  input  C,
  output Res,
  output Acarreo
);

  wire and_1_out, and_2_out, xor_1_out;

  xor xor_1 (xor_1_out, X, Y);
  and and_1 (and_1_out, xor_1_out, C);
  and and_2 (and_2_out, Y, X);
  xor xor_2 (Res, xor_1_out, C);
  or or_1 (Acarreo, and_1_out, and_2_out);
endmodule

module Semisumador8bits (
  input  [7:0] X,
  input  [7:0] Y,
  output [7:0] Salida
);

  wire _1_acarreo, _2_acarreo, _3_acarreo, _4_acarreo, _6_acarreo, semisumador1bit_1_acarreo,
       semisumador1bit_3_acarreo;

  Semisumador1Bit semisumador1bit_1 (
    .X(X[0]), .Y(Y[0]), .C(1'b0), .Res(Salida[0]), .Acarreo(semisumador1bit_1_acarreo));
  Semisumador1Bit _2 (.X(X[2]), .Y(Y[2]), .C(_1_acarreo), .Res(Salida[2]), .Acarreo(_2_acarreo));
  Semisumador1Bit _4 (.X(X[4]), .Y(Y[4]), .C(_3_acarreo), .Res(Salida[4]), .Acarreo(_4_acarreo));
  Semisumador1Bit _6 (.X(X[6]), .Y(Y[6]), .C(semisumador1bit_3_acarreo), .Res(Salida[6]), .Acarreo(_6_acarreo));
  Semisumador1Bit semisumador1bit_2 (.X(X[7]), .Y(Y[7]), .C(_6_acarreo), .Res(Salida[7]));  // open: Acarreo
  Semisumador1Bit _1 (.X(X[1]), .Y(Y[1]), .C(semisumador1bit_1_acarreo), .Res(Salida[1]), .Acarreo(_1_acarreo));
  Semisumador1Bit _3 (.X(X[3]), .Y(Y[3]), .C(_2_acarreo), .Res(Salida[3]), .Acarreo(_3_acarreo));
  Semisumador1Bit semisumador1bit_3 (
    .X(X[5]), .Y(Y[5]), .C(_4_acarreo), .Res(Salida[5]), .Acarreo(semisumador1bit_3_acarreo));

  // Notes on the sheet:
  //   0
  //   0
  //   5
  //   7
endmodule
